# Fritzing sketch GetStarted (saved by Fritzing 0.9.2b)
breadboards: 1

parts:
  Raspberry_Pi1 = Raspberry Pi 2
  Grove1 = Grove Temperature Sensor

nets:
  3V3: Raspberry_Pi1.3v3, Grove1.VCC
  N1: Raspberry_Pi1.GPIO4, Grove1.SIG
  GND: Raspberry_Pi1.GND, Grove1.GND
