# Fritzing sketch Scenario1 (saved by Fritzing 0.9.2b)
breadboards: 1

parts:
  Raspberry_Pi2 = Raspberry Pi 2
  LED1 = LED - 5mm [color="Red (633nm)" package="5 mm [THT]"]

nets:
  N1: Raspberry_Pi2.3v3, LED1.anode
  N2: Raspberry_Pi2.GPIO9, LED1.cathode
