# Fritzing sketch Scenario2 (saved by Fritzing 0.9.2b)
breadboards: 1

parts:
  Raspberry_Pi2 = Raspberry Pi 2
  LED1 = LED - 5mm [color="Red (633nm)" package="5 mm [THT]"]
  LED2 = LED - 5mm [color="Green (555nm)" package="5 mm [THT]"]

nets:
  N1: Raspberry_Pi2.3v3, LED1.anode, LED2.anode
  N2: Raspberry_Pi2.GPIO27, LED1.cathode
  N3: Raspberry_Pi2.GPIO22, LED2.cathode
