# Fritzing sketch Scenario3 (saved by Fritzing 0.9.2b)
breadboards: 1

parts:
  Raspberry_Pi1 = Raspberry Pi 2
  Grove1 = Grove Temperature Sensor
  LED1 = LED - 5mm [color="Red (633nm)" package="5 mm [THT]"]

nets:
  3V3: Raspberry_Pi1.3v3, Grove1.VCC, LED1.anode
  N1: Raspberry_Pi1.GPIO4, Grove1.SIG
  N2: Raspberry_Pi1.GPIO27, LED1.cathode
  GND: Raspberry_Pi1.GND, Grove1.GND
